// Logisim project Lab2Solution.circ as structural Verilog: 1 circuit, main circuit main
module main (
  input  O1,
  input  O0,
  input  S,
  input  A1,
  input  A0,
  input  B1,
  input  B0,
  output E,
  output G,
  output L,
  output B,
  output L0,
  output L1,
  output L2,
  output L3,
  output L4,
  output L5,
  output L6,
  output L7,
  output N
);

  wire and_1_out, and_2_out, and_3_out, and_4_out, and_5_out, and_6_out, and_7_out, and_8_out, and_9_out,
       and_10_out, and_11_out, and_12_out, and_13_out, and_14_out, and_15_out, and_16_out, and_17_out,
       and_18_out, and_19_out, and_20_out, and_21_out, and_22_out, and_23_out, and_24_out, and_25_out,
       and_26_out, and_27_out, and_28_out, and_29_out, n3_to_8_decoder_74138_1_p7,
       n3_to_8_decoder_74138_1_p8, n3_to_8_decoder_74138_1_p9, n3_to_8_decoder_74138_1_p10,
       n3_to_8_decoder_74138_1_p11, n3_to_8_decoder_74138_1_p12, n3_to_8_decoder_74138_1_p13,
       n3_to_8_decoder_74138_1_p14, n3_to_8_decoder_74138_2_p7, n3_to_8_decoder_74138_2_p8,
       n3_to_8_decoder_74138_2_p9, n3_to_8_decoder_74138_2_p10, n3_to_8_decoder_74138_2_p11,
       n3_to_8_decoder_74138_2_p12, n3_to_8_decoder_74138_2_p13, n3_to_8_decoder_74138_2_p14,
       n3_to_8_decoder_74138_3_p7, n3_to_8_decoder_74138_3_p8, n3_to_8_decoder_74138_3_p9,
       n3_to_8_decoder_74138_3_p10, n3_to_8_decoder_74138_3_p11, n3_to_8_decoder_74138_3_p12,
       n3_to_8_decoder_74138_3_p13, n3_to_8_decoder_74138_3_p14, n4_to_1_mux_x2_74153_1_p7, not_1_out,
       not_2_out, not_3_out, not_4_out, not_5_out, not_6_out, not_7_out, not_8_out, not_9_out, not_10_out,
       not_11_out, not_12_out, not_13_out, not_14_out, not_15_out, not_16_out, not_17_out, not_18_out,
       not_19_out, not_20_out, not_21_out, not_22_out, not_23_out, not_24_out, not_25_out, not_26_out,
       not_27_out, not_28_out, not_29_out, not_30_out, not_31_out, not_32_out, not_33_out, not_34_out,
       not_35_out, or_1_out, or_2_out, or_3_out, or_4_out, or_5_out, or_6_out, or_7_out, or_8_out, or_9_out,
       or_10_out, or_11_out, or_12_out, xnor_1_out, xnor_2_out, xor_1_out, xor_2_out, xor_3_out;

  not not_1 (not_1_out, A1);
  not not_2 (not_2_out, A0);
  not not_3 (not_3_out, B1);
  not not_4 (not_4_out, B0);
  not not_5 (not_5_out, A1);
  not not_6 (not_6_out, A0);
  // _3_to_8_decoder__74138 #(.Facing("east")) 3_to_8_decoder_74138_1: pin names not known; wires that end beside it: O0, O1, S, 1'b1, 1'b0, 1'b0, n3_to_8_decoder_74138_1_p7, n3_to_8_decoder_74138_1_p8, n3_to_8_decoder_74138_1_p9, n3_to_8_decoder_74138_1_p10, n3_to_8_decoder_74138_1_p11, n3_to_8_decoder_74138_1_p12, n3_to_8_decoder_74138_1_p13, n3_to_8_decoder_74138_1_p14
  xor xor_1 (xor_1_out, A1, B1);
  not not_7 (not_7_out, A1);
  not not_8 (not_8_out, A0);
  xor xor_2 (xor_2_out, A0, B0);
  and and_1 (and_1_out, A0, B0);
  xor xor_3 (xor_3_out, xor_1_out, and_1_out);
  and and_2 (and_2_out, and_1_out, xor_1_out);
  or or_1 (or_1_out, and_2_out, and_3_out);
  and and_3 (and_3_out, A1, B1);
  not not_9 (not_9_out, n3_to_8_decoder_74138_1_p7);
  not not_10 (not_10_out, n3_to_8_decoder_74138_1_p8);
  not not_11 (not_11_out, n3_to_8_decoder_74138_1_p9);
  not not_12 (not_12_out, n3_to_8_decoder_74138_1_p10);
  not not_13 (not_13_out, n3_to_8_decoder_74138_1_p11);
  not not_14 (not_14_out, n3_to_8_decoder_74138_1_p12);
  not not_15 (not_15_out, n3_to_8_decoder_74138_1_p13);
  not not_16 (not_16_out, n3_to_8_decoder_74138_1_p14);
  not not_17 (not_17_out, A1);
  xnor xnor_1 (xnor_1_out, A1, B1);
  xnor xnor_2 (xnor_2_out, A0, B0);
  // _4_to_1_MUX__x2___74153 #(.Facing("east")) 4_to_1_mux_x2_74153_1: pin names not known; wires that end beside it: A0, A1, 1'b0, B0, 1'b0, 1'b0, n4_to_1_mux_x2_74153_1_p7
  and and_4 (and_4_out, not_5_out, not_6_out);
  and and_5 (and_5_out, not_5_out, A0);
  and and_6 (and_6_out, A1, not_6_out);
  and and_7 (and_7_out, A1, A0);
  // _3_to_8_decoder__74138 #(.Facing("east")) 3_to_8_decoder_74138_2: pin names not known; wires that end beside it: xor_2_out, xor_3_out, or_1_out, 1'b1, 1'b0, 1'b0, n3_to_8_decoder_74138_2_p7, n3_to_8_decoder_74138_2_p8, n3_to_8_decoder_74138_2_p9, n3_to_8_decoder_74138_2_p10, n3_to_8_decoder_74138_2_p11, n3_to_8_decoder_74138_2_p12, n3_to_8_decoder_74138_2_p13, n3_to_8_decoder_74138_2_p14
  and and_8 (and_8_out, not_1_out, not_2_out);
  and and_9 (and_9_out, not_1_out, B1);
  and and_10 (and_10_out, A1, not_3_out);
  and and_11 (and_11_out, A1, A0);
  and and_12 (and_12_out, not_2_out, B0);
  and and_13 (and_13_out, A0, not_4_out);
  and and_14 (and_14_out, not_1_out, B1);
  and and_15 (and_15_out, not_1_out, not_2_out);
  and and_16 (and_16_out, not_2_out, B1);
  assign L0 = or_12_out ? 1'b0 : 1'bz;  // Controlled_Buffer controlled_buffer_1
  assign L1 = or_12_out ? 1'b0 : 1'bz;  // Controlled_Buffer controlled_buffer_2
  assign L2 = or_12_out ? 1'b0 : 1'bz;  // Controlled_Buffer controlled_buffer_3
  assign L3 = or_12_out ? 1'b0 : 1'bz;  // Controlled_Buffer controlled_buffer_4
  assign L4 = or_12_out ? 1'b0 : 1'bz;  // Controlled_Buffer controlled_buffer_5
  assign L5 = or_12_out ? 1'b0 : 1'bz;  // Controlled_Buffer controlled_buffer_6
  assign L6 = or_12_out ? 1'b0 : 1'bz;  // Controlled_Buffer controlled_buffer_7
  assign L7 = or_12_out ? 1'b0 : 1'bz;  // Controlled_Buffer controlled_buffer_8
  assign L1 = not_15_out ? 1'b0 : 1'bz;  // Controlled_Buffer controlled_buffer_9
  assign L3 = not_15_out ? 1'b0 : 1'bz;  // Controlled_Buffer controlled_buffer_10
  assign L5 = not_15_out ? 1'b0 : 1'bz;  // Controlled_Buffer controlled_buffer_11
  assign L7 = not_15_out ? 1'b0 : 1'bz;  // Controlled_Buffer controlled_buffer_12
  assign L2 = not_11_out ? not_15_out : 1'bz;  // Controlled_Buffer controlled_buffer_13
  assign L3 = not_11_out ? not_15_out : 1'bz;  // Controlled_Buffer controlled_buffer_14
  assign L4 = not_11_out ? not_15_out : 1'bz;  // Controlled_Buffer controlled_buffer_15
  assign L5 = not_11_out ? not_15_out : 1'bz;  // Controlled_Buffer controlled_buffer_16
  assign L6 = not_11_out ? not_15_out : 1'bz;  // Controlled_Buffer controlled_buffer_17
  assign L7 = not_11_out ? not_15_out : 1'bz;  // Controlled_Buffer controlled_buffer_18
  and and_17 (and_17_out, xnor_1_out, xnor_2_out);
  and and_18 (and_18_out, not_7_out, B1);
  and and_19 (and_19_out, not_7_out, not_8_out);
  assign L0 = not_11_out ? not_17_out : 1'bz;  // Controlled_Buffer controlled_buffer_19
  assign L1 = not_11_out ? A1 : 1'bz;  // Controlled_Buffer controlled_buffer_20
  assign L0 = not_15_out ? and_4_out : 1'bz;  // Controlled_Buffer controlled_buffer_21
  assign L2 = not_15_out ? and_5_out : 1'bz;  // Controlled_Buffer controlled_buffer_22
  assign L4 = not_15_out ? and_6_out : 1'bz;  // Controlled_Buffer controlled_buffer_23
  assign L6 = not_15_out ? and_7_out : 1'bz;  // Controlled_Buffer controlled_buffer_24
  and and_20 (and_20_out, and_8_out, B1);
  and and_21 (and_21_out, and_9_out, B0);
  and and_22 (and_22_out, and_10_out, not_4_out);
  and and_23 (and_23_out, and_11_out, not_3_out);
  or or_2 (or_2_out, and_12_out, and_13_out);
  and and_24 (and_24_out, and_15_out, B0);
  and and_25 (and_25_out, and_16_out, B0);
  and and_26 (and_26_out, and_19_out, B0);
  and and_27 (and_27_out, not_8_out, B1);
  not not_18 (not_18_out, n3_to_8_decoder_74138_2_p7);
  not not_19 (not_19_out, n3_to_8_decoder_74138_2_p8);
  not not_20 (not_20_out, n3_to_8_decoder_74138_2_p9);
  not not_21 (not_21_out, n3_to_8_decoder_74138_2_p10);
  not not_22 (not_22_out, n3_to_8_decoder_74138_2_p11);
  not not_23 (not_23_out, n3_to_8_decoder_74138_2_p12);
  not not_24 (not_24_out, n3_to_8_decoder_74138_2_p13);
  not not_25 (not_25_out, n3_to_8_decoder_74138_2_p14);
  or or_3 (or_3_out, and_20_out, and_21_out);
  or or_4 (or_4_out, and_22_out, and_23_out);
  or or_5 (or_5_out, and_14_out, or_6_out);
  or or_6 (or_6_out, and_24_out, and_25_out);
  and and_28 (and_28_out, and_27_out, B0);
  assign L0 = not_12_out ? not_18_out : 1'bz;  // Controlled_Buffer controlled_buffer_25
  assign L1 = not_12_out ? not_19_out : 1'bz;  // Controlled_Buffer controlled_buffer_26
  assign L2 = not_12_out ? not_20_out : 1'bz;  // Controlled_Buffer controlled_buffer_27
  assign L3 = not_12_out ? not_21_out : 1'bz;  // Controlled_Buffer controlled_buffer_28
  assign L4 = not_12_out ? not_22_out : 1'bz;  // Controlled_Buffer controlled_buffer_29
  assign L5 = not_12_out ? not_23_out : 1'bz;  // Controlled_Buffer controlled_buffer_30
  assign L6 = not_12_out ? not_24_out : 1'bz;  // Controlled_Buffer controlled_buffer_31
  assign L7 = not_12_out ? not_25_out : 1'bz;  // Controlled_Buffer controlled_buffer_32
  or or_7 (or_7_out, or_3_out, or_4_out);
  or or_8 (or_8_out, and_18_out, or_9_out);
  or or_9 (or_9_out, and_26_out, and_28_out);
  // _3_to_8_decoder__74138 #(.Facing("east")) 3_to_8_decoder_74138_3: pin names not known; wires that end beside it: or_2_out, or_7_out, 1'b0, 1'b1, 1'b0, 1'b0, n3_to_8_decoder_74138_3_p7, n3_to_8_decoder_74138_3_p8, n3_to_8_decoder_74138_3_p9, n3_to_8_decoder_74138_3_p10, n3_to_8_decoder_74138_3_p11, n3_to_8_decoder_74138_3_p12, n3_to_8_decoder_74138_3_p13, n3_to_8_decoder_74138_3_p14
  or or_10 (or_10_out, not_10_out, not_14_out);
  not not_26 (not_26_out, n3_to_8_decoder_74138_3_p7);
  not not_27 (not_27_out, n3_to_8_decoder_74138_3_p8);
  not not_28 (not_28_out, n3_to_8_decoder_74138_3_p9);
  not not_29 (not_29_out, n3_to_8_decoder_74138_3_p10);
  not not_30 (not_30_out, n3_to_8_decoder_74138_3_p11);
  not not_31 (not_31_out, n3_to_8_decoder_74138_3_p12);
  not not_32 (not_32_out, n3_to_8_decoder_74138_3_p13);
  not not_33 (not_33_out, n3_to_8_decoder_74138_3_p14);
  assign L0 = not_16_out ? not_26_out : 1'bz;  // Controlled_Buffer controlled_buffer_33
  assign L1 = not_16_out ? not_27_out : 1'bz;  // Controlled_Buffer controlled_buffer_34
  assign L2 = not_16_out ? not_28_out : 1'bz;  // Controlled_Buffer controlled_buffer_35
  assign L3 = not_16_out ? not_29_out : 1'bz;  // Controlled_Buffer controlled_buffer_36
  assign L4 = not_16_out ? not_30_out : 1'bz;  // Controlled_Buffer controlled_buffer_37
  assign L5 = not_16_out ? not_31_out : 1'bz;  // Controlled_Buffer controlled_buffer_38
  assign L6 = not_16_out ? not_32_out : 1'bz;  // Controlled_Buffer controlled_buffer_39
  assign L7 = not_16_out ? not_33_out : 1'bz;  // Controlled_Buffer controlled_buffer_40
  or or_11 (or_11_out, not_9_out, not_13_out);
  not not_34 (not_34_out, and_17_out);
  and and_29 (and_29_out, not_34_out, not_35_out);
  not not_35 (not_35_out, or_8_out);
  or or_12 (or_12_out, or_11_out, or_10_out);
  and and_30 (E, or_11_out, and_17_out);
  and and_31 (G, or_11_out, and_29_out);
  and and_32 (L, or_11_out, or_8_out);
  and and_33 (B, or_10_out, n4_to_1_mux_x2_74153_1_p7);
  and and_34 (N, or_5_out, not_16_out);

  // Notes on the sheet:
  //   To keep L2, L3, L4, L5, L6, L7 as 0 for A/2 operation
  //   To keep L1, L3, L5, L7 as 0 for A*2 operation
  //   A+B
  //   To keep number outputs as 0 for Number Comparison and Bit Select
  //   A == B
  //   A*2
  //   A/2
  //   A<B
  //   A-B
  //   A>B
endmodule
