// Logisim project e2380947.circ as structural Verilog: 1 circuit, main circuit main
module main (
  input  A1,
  input  A0,
  input  B1,
  input  B0,
  input  O1,
  input  O0,
  input  S,
  output E,
  output G,
  output L,
  output N,
  output B,
  output L0,
  output L1,
  output L2,
  output L4,
  output L6,
  output L3,
  output L5,
  output L7
);

  wire and_1_out, and_3_out, and_4_out, and_5_out, and_6_out, and_7_out, and_8_out, and_9_out, and_10_out,
       and_11_out, and_12_out, and_13_out, and_14_out, and_15_out, and_16_out, and_17_out, and_18_out,
       and_19_out, and_20_out, and_21_out, and_22_out, and_23_out, and_24_out, and_25_out, and_26_out,
       and_27_out, and_28_out, and_29_out, and_30_out, and_31_out, and_32_out, and_33_out, and_34_out,
       and_35_out, and_36_out, and_37_out, and_39_out, and_42_out, and_43_out, and_44_out, and_47_out,
       and_48_out, and_49_out, and_50_out, and_51_out, and_52_out, and_53_out, n4_to_1_mux_x2_74153_1_p9,
       n4_to_1_mux_x2_74153_2_p13, n4_to_1_mux_x2_74153_2_p14, nor_1_out, not_1_out, not_3_out, not_4_out,
       not_5_out, not_6_out, not_7_out, not_8_out, not_13_out, not_14_out, not_15_out, not_16_out,
       not_17_out, not_18_out, not_19_out, not_20_out, not_21_out, not_22_out, not_23_out, not_24_out,
       not_25_out, not_26_out, not_27_out, not_28_out, not_29_out, not_30_out, not_31_out, or_1_out,
       or_2_out, or_3_out, or_4_out, or_5_out, or_6_out, or_7_out, or_8_out, or_9_out, or_10_out, or_11_out,
       or_12_out, or_13_out, or_14_out, or_15_out, or_16_out, or_17_out, or_18_out, or_19_out, or_20_out,
       or_21_out;

  not not_1 (not_1_out, A1);
  // NOT_Gate not_2 has open pins: in=A0, out=open
  not not_3 (not_3_out, B1);
  not not_4 (not_4_out, B0);
  // _3_to_8_decoder__74138 #(.Facing("east")) 3_to_8_decoder_74138_1: pin names not known; wires that end beside it: A0, A1, 1'b0, 1'b1, 1'b0, 1'b0
  // _3_to_8_decoder__74138 #(.Facing("east")) 3_to_8_decoder_74138_2: pin names not known; wires that end beside it: B0, B1, A0, 1'b1, 1'b0, 1'b0
  // _3_to_8_decoder__74138 #(.Facing("east")) 3_to_8_decoder_74138_3: pin names not known; wires that end beside it: B0, B1, A0, 1'b1, 1'b0, 1'b0
  // _4_to_1_MUX__x2___74153 #(.Facing("east")) 4_to_1_mux_x2_74153_1: pin names not known; wires that end beside it: 1'b0, not_4_out, B0, 1'b1, 1'b0, A0, 1'b0, A1, n4_to_1_mux_x2_74153_1_p9
  // NOT_Gate not_5 has open pins: in=open, out=not_5_out
  // NOT_Gate not_6 has open pins: in=open, out=not_6_out
  // NOT_Gate not_7 has open pins: in=open, out=not_7_out
  // NOT_Gate not_8 has open pins: in=open, out=not_8_out
  // NOT_Gate not_9 is placed but not wired
  // NOT_Gate not_10 is placed but not wired
  // NOT_Gate not_11 is placed but not wired
  // NOT_Gate not_12 is placed but not wired
  and and_1 (and_1_out, not_13_out, A1);
  // NOT_Gate not_13 has open pins: in=open, out=not_13_out
  // NOT_Gate not_14 has open pins: in=open, out=not_14_out
  // NOT_Gate not_15 has open pins: in=open, out=not_15_out
  // NOT_Gate not_16 has open pins: in=open, out=not_16_out
  // NOT_Gate not_17 has open pins: in=open, out=not_17_out
  // NOT_Gate not_18 has open pins: in=open, out=not_18_out
  // NOT_Gate not_19 has open pins: in=open, out=not_19_out
  // NOT_Gate not_20 has open pins: in=open, out=not_20_out
  // NOT_Gate not_21 has open pins: in=open, out=not_21_out
  // NOT_Gate not_22 has open pins: in=open, out=not_22_out
  // NOT_Gate not_23 has open pins: in=open, out=not_23_out
  // NOT_Gate not_24 has open pins: in=open, out=not_24_out
  // NOT_Gate not_25 has open pins: in=open, out=not_25_out
  // NOT_Gate not_26 has open pins: in=open, out=not_26_out
  // NOT_Gate not_27 has open pins: in=open, out=not_27_out
  // NOT_Gate not_28 has open pins: in=open, out=not_28_out
  or or_1 (or_1_out, not_3_out, not_4_out);
  and and_2 (B, n4_to_1_mux_x2_74153_1_p9, and_43_out);
  and and_3 (and_3_out, and_13_out, S);
  and and_4 (and_4_out, and_33_out, and_5_out);
  and and_5 (and_5_out, not_1_out, not_13_out);
  or or_2 (or_2_out, not_14_out, not_17_out);
  and and_6 (and_6_out, not_20_out, not_1_out);
  or or_3 (or_3_out, not_15_out, not_18_out);
  and and_7 (and_7_out, or_3_out, A1);
  or or_4 (or_4_out, not_19_out, not_16_out);
  and and_8 (and_8_out, A1, not_20_out);
  or or_5 (or_5_out, not_27_out, not_22_out);
  or or_6 (or_6_out, not_26_out, not_21_out);
  and and_9 (and_9_out, not_3_out, not_4_out);
  and and_10 (and_10_out, B0, not_3_out);
  and and_11 (and_11_out, B1, not_4_out);
  and and_12 (and_12_out, B0, B1);
  // _4_to_1_MUX__x2___74153 #(.Facing("east")) 4_to_1_mux_x2_74153_2: pin names not known; wires that end beside it: and_9_out, and_10_out, and_11_out, and_12_out, 1'b0, and_9_out, not_3_out, or_1_out, 1'b0, A0, 1'b0, A1, n4_to_1_mux_x2_74153_2_p13, n4_to_1_mux_x2_74153_2_p14
  and and_13 (and_13_out, O1, not_30_out);
  and and_14 (and_14_out, and_13_out, not_31_out);
  and and_15 (and_15_out, and_14_out, not_1_out);
  and and_16 (and_16_out, and_14_out, A1);
  and and_17 (and_17_out, and_3_out, not_5_out);
  and and_18 (and_18_out, and_3_out, not_6_out);
  and and_19 (and_19_out, not_1_out, and_20_out);
  and and_20 (and_20_out, or_2_out, and_33_out);
  and and_21 (and_21_out, not_1_out, or_7_out);
  or or_7 (or_7_out, not_15_out, not_18_out);
  or or_8 (or_8_out, and_21_out, and_1_out);
  and and_22 (and_22_out, not_1_out, or_9_out);
  or or_9 (or_9_out, not_16_out, not_19_out);
  or or_10 (or_10_out, and_22_out, and_23_out);
  and and_23 (and_23_out, A1, or_11_out);
  or or_11 (or_11_out, not_14_out, not_17_out);
  or or_12 (or_12_out, and_6_out, and_7_out);
  and and_24 (and_24_out, A1, or_4_out);
  and and_25 (and_25_out, not_1_out, not_24_out);
  and and_26 (and_26_out, A1, not_25_out);
  and and_27 (and_27_out, not_25_out, not_1_out);
  and and_28 (and_28_out, not_24_out, A1);
  or or_13 (or_13_out, not_28_out, not_23_out);
  and and_29 (and_29_out, or_13_out, not_1_out);
  or or_14 (or_14_out, and_29_out, and_30_out);
  and and_30 (and_30_out, or_6_out, A1);
  and and_31 (and_31_out, not_29_out, not_30_out);
  not not_29 (not_29_out, O1);
  not not_30 (not_30_out, O0);
  not not_31 (not_31_out, S);
  and and_32 (and_32_out, O0, O1);
  and and_33 (and_33_out, not_31_out, and_32_out);
  and and_34 (and_34_out, and_3_out, not_7_out);
  and and_35 (and_35_out, and_33_out, or_8_out);
  and and_36 (and_36_out, and_33_out, or_10_out);
  and and_37 (and_37_out, and_33_out, or_12_out);
  and and_38 (L5, and_33_out, and_24_out);
  and and_39 (and_39_out, and_33_out, and_8_out);
  or or_15 (or_15_out, and_25_out, and_26_out);
  or or_16 (or_16_out, and_27_out, and_28_out);
  and and_40 (E, n4_to_1_mux_x2_74153_2_p13, and_31_out);
  and and_41 (G, n4_to_1_mux_x2_74153_2_p14, and_31_out);
  nor nor_1 (nor_1_out, n4_to_1_mux_x2_74153_2_p13, n4_to_1_mux_x2_74153_2_p14);
  and and_42 (and_42_out, O1, O0);
  and and_43 (and_43_out, not_29_out, O0);
  and and_44 (and_44_out, and_3_out, not_8_out);
  or or_17 (or_17_out, or_16_out, or_5_out);
  and and_45 (L, nor_1_out, and_31_out);
  and and_46 (N, nor_1_out, and_47_out);
  and and_47 (and_47_out, and_42_out, S);
  and and_48 (and_48_out, O1, O0);
  or or_18 (or_18_out, and_15_out, and_17_out);
  or or_19 (or_19_out, and_16_out, and_19_out);
  and and_49 (and_49_out, S, and_48_out);
  and and_50 (and_50_out, and_49_out, n4_to_1_mux_x2_74153_2_p13);
  or or_20 (or_20_out, or_18_out, and_4_out);
  or or_21 (or_21_out, and_18_out, and_35_out);
  or or_22 (L6, and_39_out, and_44_out);
  or or_23 (L0, and_50_out, or_20_out);
  and and_51 (and_51_out, and_49_out, or_17_out);
  or or_24 (L1, and_51_out, or_19_out);
  and and_52 (and_52_out, and_49_out, or_14_out);
  or or_25 (L4, and_34_out, and_37_out);
  or or_26 (L2, or_21_out, and_52_out);
  and and_53 (and_53_out, and_49_out, or_15_out);
  or or_27 (L3, and_36_out, and_53_out);

  assign L7 = 1'b0;
endmodule
